// Logisim project test.circ as structural Verilog: 12 circuits, main circuit main
module main (
  input  in_1,
  output [5:0] func,
  output [5:0] opcode
);

  wire ALUSrc, Available, Branch, clk, \final , MemToReg, MemWrite, PCSrc_out, RegDst, RegWrite, ZERO;
  wire [1:0] ALUOp_1_0, ExtOp_1_0;
  wire [4:0] ifu_1_pc_address, multiplexer_1_out, \rs源1 , \rt源2 ;
  wire [15:6] Imm;
  wire [31:0] alu_1_result, extender_1_ext32, multiplexer_2_out, multiplexer_3_out, ram_1_data,
       \regfile_1_d1读出的寄存器数据 , \regfile_1_d2读出的寄存器数据 ;

  Clock clock_1 (.out(clk));
  and PCSrc (PCSrc_out, ZERO, Branch);
  IFU ifu_1 (
    .PCSrc(PCSrc_out), .\reset复位 (in_1), .\输出到main_取出的指令 ({opcode, \rs源1 , \rt源2 , Imm, func}),
    .\clk时钟 (clk), .PC_Address(ifu_1_pc_address));
  // Probe on {opcode, \rs源1 , \rt源2 , Imm, func}
  // Probe on ifu_1_pc_address
  // Probe on ifu_1_pc_address
  // Probe on {opcode, \rs源1 , \rt源2 , Imm, func}
  Comparator #(.width(32)) comparator_1 (
    .a({opcode, \rs源1 , \rt源2 , Imm, func}), .b({32{1'b0}}), .eq(\final ));  // open: gt, lt
  Multiplexer #(.width(5)) multiplexer_1 (
    .in0(\rt源2 ), .in1(Imm[15:11]), .out(multiplexer_1_out), .sel(RegDst));  // open: en
  Extender extender_1 (.imm16({Imm, func}), .ExtOp_1_0(ExtOp_1_0), .ext32(extender_1_ext32));
  RegFile regfile_1 (
    .clk(clk), .\A1_读寄存器 (\rs源1 ), .\A2_读寄存器 (\rt源2 ), .\A3_写寄存器 (multiplexer_1_out),
    .\WD要写的数据 (multiplexer_3_out), .\D1读出的寄存器数据 (\regfile_1_d1读出的寄存器数据 ),
    .\D2读出的寄存器数据 (\regfile_1_d2读出的寄存器数据 ), .RegWrite(RegWrite));
  Controller controller_1 (
    .func(func), .opcode(opcode), .RegDst(RegDst), .ALUSrc(ALUSrc), .MemtoReg(MemToReg), .RegWrite(RegWrite),
    .Memread(Available), .MemWrite(MemWrite), .Branch(Branch), .ALUOp_1_0(ALUOp_1_0), .ExtOp_1_0(ExtOp_1_0));
  Multiplexer #(.width(32)) multiplexer_2 (
    .in0(\regfile_1_d2读出的寄存器数据 ), .in1(extender_1_ext32), .out(multiplexer_2_out), .sel(ALUSrc));  // open: en
  Multiplexer #(.width(32)) multiplexer_3 (
    .in0(alu_1_result), .in1(ram_1_data), .out(multiplexer_3_out), .sel(MemToReg));  // open: en
  ALU alu_1 (
    .A(\regfile_1_d1读出的寄存器数据 ), .B(multiplexer_2_out), .ALUOp(ALUOp_1_0), .\判断ALU输出是否为0 (ZERO),
    .Result(alu_1_result));
  RAM #(.addrWidth(5), .dataWidth(32), .bus("separate")) ram_1 (
    .addr(alu_1_result[4:0]), .din(\regfile_1_d2读出的寄存器数据 ), .data(ram_1_data), .str(MemWrite), .clk(clk),
    .clr(in_1));  // open: sel, ld

  // Other names for the same wires on the sheet: Imm[5:0] = func; shamt[4:0] = Imm[10:6]; rd[4:0] = Imm[15:11];
  //   reset = in_1

  // Notes on the sheet:
  //   低
  //   func
  //   shamt
  //   rd
  //   rt
  //   rs
  //   opcode
  //   高
  //   address
  //   r指令时指出alu功能
  //   寄存器文件
  //   ↑要写入寄存器的数据
  //   ←要写入寄存器的数据
  //   寄存器读出的数据2
  //   指令低16位的符号拓展
  //   寄存器读出的数据2→送往内存单元
  //   控制Extender的拓展方式
  //   2 bit 控制ALU的运算
  //   与ALU0输出结合决定PC是否跳转
  //   将数据写入到指定存储器单元中
  //   待定指令
  //   寄存器写使能有效
  //   写入寄存器的数据来源
  //   第二个ALU操作数的来源
  //   写寄存器的目标寄存器号来源
  //   RAM(DM)
endmodule

module ALU (
  input  [31:0] A,
  input  [31:0] B,
  input  [1:0] ALUOp,
  output \判断ALU输出是否为0 ,
  output [31:0] Result
);

  wire [31:0] _32_bit_Adder_sum, _32_bit_ori_out_3, _32_bit_substract_out_3;

  adder_32bit _32_bit_Adder (.B(B), .A(A), .Sum(_32_bit_Adder_sum));
  substract_32bit _32_bit_substract (.\A被减数 (A), .\B减数 (B), .out_3(_32_bit_substract_out_3));
  ori_32bit _32_bit_ori (.A(A), .B(B), .out_3(_32_bit_ori_out_3));
  Multiplexer #(.select(2), .width(32)) multiplexer_1 (
    .in0(_32_bit_Adder_sum), .in1(_32_bit_substract_out_3), .in2(_32_bit_ori_out_3), .out(Result), .sel(ALUOp));  // open: in3, en
  Comparator #(.width(32)) comparator_1 (.a(Result), .b({32{1'b0}}), .eq(\判断ALU输出是否为0 ));  // open: gt, lt

  // Notes on the sheet:
  //   alu控制信号 控制输出哪一个结果
  //   0 0 add
  //   0 1 sub
  //   1 0 or
endmodule

module adder_32bit (
  input  [31:0] B,
  input  [31:0] A,
  output [31:0] Sum
);

  wire \_0_c进位 , \_1_进位c_i_1 , \_2_进位c_i_1 , \_3_进位c_i_1 , \_4_进位c_i_1 , \_5_进位c_i_1 , \_6_进位c_i_1 ,
       \_7_进位c_i_1 , \_8_进位c_i_1 , \_9_进位c_i_1 , \_10_进位c_i_1 , \_11_进位c_i_1 , \_12_进位c_i_1 , \_13_进位c_i_1 ,
       \_14_进位c_i_1 , \_15_进位c_i_1 , \_16_进位c_i_1 , \_17_进位c_i_1 , \_18_进位c_i_1 , \_19_进位c_i_1 ,
       \_20_进位c_i_1 , \_21_进位c_i_1 , \_22_进位c_i_1 , \_23_进位c_i_1 , \_24_进位c_i_1 , \_25_进位c_i_1 ,
       \_26_进位c_i_1 , \_27_进位c_i_1 , \_28_进位c_i_1 , \_29_进位c_i_1 , \_30_进位c_i_1 ;

  \_1位全加器  _31 (.a_i(A[31]), .b_i(B[31]), .c_i(\_30_进位c_i_1 ), .\结果s_i (Sum[31]));  // open: 进位c_i_1
  \_1位全加器  _30 (.a_i(A[30]), .b_i(B[30]), .c_i(\_29_进位c_i_1 ), .\结果s_i (Sum[30]), .\进位c_i_1 (\_30_进位c_i_1 ));
  \_1位全加器  _29 (.a_i(A[29]), .b_i(B[29]), .c_i(\_28_进位c_i_1 ), .\结果s_i (Sum[29]), .\进位c_i_1 (\_29_进位c_i_1 ));
  \_1位全加器  _28 (.a_i(A[28]), .b_i(B[28]), .c_i(\_27_进位c_i_1 ), .\结果s_i (Sum[28]), .\进位c_i_1 (\_28_进位c_i_1 ));
  \_1位全加器  _27 (.a_i(A[27]), .b_i(B[27]), .c_i(\_26_进位c_i_1 ), .\结果s_i (Sum[27]), .\进位c_i_1 (\_27_进位c_i_1 ));
  \_1位全加器  _26 (.a_i(A[26]), .b_i(B[26]), .c_i(\_25_进位c_i_1 ), .\结果s_i (Sum[26]), .\进位c_i_1 (\_26_进位c_i_1 ));
  \_1位全加器  _25 (.a_i(A[25]), .b_i(B[25]), .c_i(\_24_进位c_i_1 ), .\结果s_i (Sum[25]), .\进位c_i_1 (\_25_进位c_i_1 ));
  \_1位全加器  _24 (.a_i(A[24]), .b_i(B[24]), .c_i(\_23_进位c_i_1 ), .\结果s_i (Sum[24]), .\进位c_i_1 (\_24_进位c_i_1 ));
  \_1位全加器  _23 (.a_i(A[23]), .b_i(B[23]), .c_i(\_22_进位c_i_1 ), .\结果s_i (Sum[23]), .\进位c_i_1 (\_23_进位c_i_1 ));
  \_1位全加器  _22 (.a_i(A[22]), .b_i(B[22]), .c_i(\_21_进位c_i_1 ), .\结果s_i (Sum[22]), .\进位c_i_1 (\_22_进位c_i_1 ));
  \_1位全加器  _21 (.a_i(A[21]), .b_i(B[21]), .c_i(\_20_进位c_i_1 ), .\结果s_i (Sum[21]), .\进位c_i_1 (\_21_进位c_i_1 ));
  \_1位全加器  _20 (.a_i(A[20]), .b_i(B[20]), .c_i(\_19_进位c_i_1 ), .\结果s_i (Sum[20]), .\进位c_i_1 (\_20_进位c_i_1 ));
  \_1位全加器  _19 (.a_i(A[19]), .b_i(B[19]), .c_i(\_18_进位c_i_1 ), .\结果s_i (Sum[19]), .\进位c_i_1 (\_19_进位c_i_1 ));
  \_1位全加器  _18 (.a_i(A[18]), .b_i(B[18]), .c_i(\_17_进位c_i_1 ), .\结果s_i (Sum[18]), .\进位c_i_1 (\_18_进位c_i_1 ));
  \_1位全加器  _17 (.a_i(A[17]), .b_i(B[17]), .c_i(\_16_进位c_i_1 ), .\结果s_i (Sum[17]), .\进位c_i_1 (\_17_进位c_i_1 ));
  \_1位全加器  _16 (.a_i(A[16]), .b_i(B[16]), .c_i(\_15_进位c_i_1 ), .\结果s_i (Sum[16]), .\进位c_i_1 (\_16_进位c_i_1 ));
  \_1位全加器  _15 (.a_i(A[15]), .b_i(B[15]), .c_i(\_14_进位c_i_1 ), .\结果s_i (Sum[15]), .\进位c_i_1 (\_15_进位c_i_1 ));
  \_1位全加器  _14 (.a_i(A[14]), .b_i(B[14]), .c_i(\_13_进位c_i_1 ), .\结果s_i (Sum[14]), .\进位c_i_1 (\_14_进位c_i_1 ));
  \_1位全加器  _13 (.a_i(A[13]), .b_i(B[13]), .c_i(\_12_进位c_i_1 ), .\结果s_i (Sum[13]), .\进位c_i_1 (\_13_进位c_i_1 ));
  \_1位全加器  _12 (.a_i(A[12]), .b_i(B[12]), .c_i(\_11_进位c_i_1 ), .\结果s_i (Sum[12]), .\进位c_i_1 (\_12_进位c_i_1 ));
  \_1位全加器  _11 (.a_i(A[11]), .b_i(B[11]), .c_i(\_10_进位c_i_1 ), .\结果s_i (Sum[11]), .\进位c_i_1 (\_11_进位c_i_1 ));
  \_1位全加器  _10 (.a_i(A[10]), .b_i(B[10]), .c_i(\_9_进位c_i_1 ), .\结果s_i (Sum[10]), .\进位c_i_1 (\_10_进位c_i_1 ));
  \_1位全加器  _9 (.a_i(A[9]), .b_i(B[9]), .c_i(\_8_进位c_i_1 ), .\结果s_i (Sum[9]), .\进位c_i_1 (\_9_进位c_i_1 ));
  \_1位全加器  _8 (.a_i(A[8]), .b_i(B[8]), .c_i(\_7_进位c_i_1 ), .\结果s_i (Sum[8]), .\进位c_i_1 (\_8_进位c_i_1 ));
  \_1位全加器  _7 (.a_i(A[7]), .b_i(B[7]), .c_i(\_6_进位c_i_1 ), .\结果s_i (Sum[7]), .\进位c_i_1 (\_7_进位c_i_1 ));
  \_1位全加器  _6 (.a_i(A[6]), .b_i(B[6]), .c_i(\_5_进位c_i_1 ), .\结果s_i (Sum[6]), .\进位c_i_1 (\_6_进位c_i_1 ));
  \_1位全加器  _5 (.a_i(A[5]), .b_i(B[5]), .c_i(\_4_进位c_i_1 ), .\结果s_i (Sum[5]), .\进位c_i_1 (\_5_进位c_i_1 ));
  \_1位全加器  _4 (.a_i(A[4]), .b_i(B[4]), .c_i(\_3_进位c_i_1 ), .\结果s_i (Sum[4]), .\进位c_i_1 (\_4_进位c_i_1 ));
  \_1位全加器  _3 (.a_i(A[3]), .b_i(B[3]), .c_i(\_2_进位c_i_1 ), .\结果s_i (Sum[3]), .\进位c_i_1 (\_3_进位c_i_1 ));
  \_1位全加器  _2 (.a_i(A[2]), .b_i(B[2]), .c_i(\_1_进位c_i_1 ), .\结果s_i (Sum[2]), .\进位c_i_1 (\_2_进位c_i_1 ));
  \_1位全加器  _1 (.a_i(A[1]), .b_i(B[1]), .c_i(\_0_c进位 ), .\结果s_i (Sum[1]), .\进位c_i_1 (\_1_进位c_i_1 ));
  \_1位半加器  _0 (.A(B[0]), .B(A[0]), .\sum和 (Sum[0]), .\C进位 (\_0_c进位 ));

  // Other names for the same wires on the sheet: s0 = Sum[0]; s1 = Sum[1]; s2 = Sum[2]; s3 = Sum[3]; s4 = Sum[4];
  //   s5 = Sum[5]; s6 = Sum[6]; s7 = Sum[7]; s8 = Sum[8]; s9 = Sum[9]; s10 = Sum[10]; s11 = Sum[11]; s12 = Sum[12];
  //   s13 = Sum[13]; s14 = Sum[14]; s15 = Sum[15]; s16 = Sum[16]; s17 = Sum[17]; s18 = Sum[18]; s19 = Sum[19];
  //   s20 = Sum[20]; s21 = Sum[21]; s22 = Sum[22]; s23 = Sum[23]; s24 = Sum[24]; s25 = Sum[25]; s26 = Sum[26];
  //   s27 = Sum[27]; s28 = Sum[28]; s29 = Sum[29]; s30 = Sum[30]; s31 = Sum[31]
endmodule

module \_1位全加器  (
  input  a_i,
  input  b_i,
  input  c_i,
  output \结果s_i ,
  output \进位c_i_1 
);

  xor xor_1 (\结果s_i , a_i, b_i, c_i);
  \判断进位  \u_判断进位_1  (.in_1(a_i), .in_2(b_i), .in_3(c_i), .out_4(\进位c_i_1 ));

  // Notes on the sheet:
  //   判断是否进位
endmodule

module \_1位半加器  (
  input  A,
  input  B,
  output \sum和 ,
  output \C进位 
);

  xor xor_1 (\sum和 , A, B);
  and and_1 (\C进位 , A, B);

  // Notes on the sheet:
  //   1 bit adder
  //   半加器 两个1位2进制数相加不考虑低位进位
endmodule

module \判断进位  (
  input  in_1,
  input  in_2,
  input  in_3,
  output out_4
);

  wire and_1_out, and_2_out, and_3_out;

  and and_1 (and_1_out, in_1, in_2);
  and and_2 (and_2_out, in_1, in_3);
  and and_3 (and_3_out, in_2, in_3);
  or or_1 (out_4, and_1_out, and_2_out, and_3_out);
endmodule

module substract_32bit (
  input  [31:0] \A被减数 ,
  input  [31:0] \B减数 ,
  output [31:0] out_3
);

  wire [31:0] _32_bit_Adder_sum, not_1_out;

  assign not_1_out = ~\B减数 ;  // NOT_Gate not_1, 32 bits wide
  adder_32bit _32_bit_Adder (.B(32'h1), .A(not_1_out), .Sum(_32_bit_Adder_sum));
  adder_32bit _32_bit_Adder_2 (.B(_32_bit_Adder_sum), .A(\A被减数 ), .Sum(out_3));

  // Notes on the sheet:
  //   A
  //   B
endmodule

module ori_32bit (
  input  [31:0] A,
  input  [31:0] B,
  output [31:0] out_3
);

  assign out_3 = A | B;  // OR_Gate or_1, 32 bits wide
endmodule

module IFU (
  input  PCSrc,
  input  \clk时钟 ,
  input  \reset复位 ,
  output [31:0] \输出到main_取出的指令 ,
  output [4:0] PC_Address
);

  wire [29:5] register_1_q;
  wire [31:0] Adder_2_sum, Adder_sum, bit_extender_1_out, multiplexer_1_out;

  Register #(.width(30)) register_1 (
    .D(multiplexer_1_out[29:0]), .Q({register_1_q, PC_Address}), .clk(\clk时钟 ), .clr(\reset复位 ));  // open: en
  adder_32bit Adder (.B(32'h1), .A({2'b00, register_1_q, PC_Address}), .Sum(Adder_sum));
  ROM #(.addrWidth(5), .dataWidth(32)) rom_1 (.addr(PC_Address), .data(\输出到main_取出的指令 ));  // open: sel
  assign bit_extender_1_out = {{16{1'b0}}, \输出到main_取出的指令 [15:0]};  // Bit_Extender bit_extender_1
  adder_32bit Adder_2 (.B(bit_extender_1_out), .A(Adder_sum), .Sum(Adder_2_sum));
  Multiplexer #(.width(32)) multiplexer_1 (
    .in0(Adder_sum), .in1(Adder_2_sum), .out(multiplexer_1_out), .sel(PCSrc));  // open: en

  // Notes on the sheet:
  //   30 bit register
  //   PC
  //   30 to 32
  //   高位补0
  //   指令地址
  //   PC+1
  //   以字寻址 所以加一即可达到加4的效果
  //   IM 指令存储器
  //   ROM 32bit*32字
  //   32 bit 指令
  //   contents of rom_1 (hex, n*v repeats v):
  //   3c010001 3c0000ff 3c020001 411821 12023 12823 34a60001 34270003 ac070000 ac070004 8c080000 8c090004
  //   11090001 1095821 1095021 0 1095821
  //   位扩展：16 to 32
  //   取偏移地址
  //   offset 16 bit
  //   以字为单位
  //   以字为单位
  //   PC+4
  //   offset
  //   PC+4+offset
  //   PC+4→
  //   PC+4+offset
  //   判断是否执行分支
  //   32 to30
endmodule

module Controller (
  input  [5:0] func,
  input  [5:0] opcode,
  output RegDst,
  output ALUSrc,
  output MemtoReg,
  output RegWrite,
  output Memread,
  output MemWrite,
  output Branch,
  output [1:0] ALUOp_1_0,
  output [1:0] ExtOp_1_0
);

  wire ADDU_out, BEQ_out, LW_out, not_1_out, not_2_out, not_3_out, not_4_out, not_5_out, not_6_out,
       not_7_out, not_8_out, not_9_out, not_10_out, not_11_out, not_12_out, ORI_out, SUBU_out, SW_out;

  not not_1 (not_1_out, func[5]);
  not not_2 (not_2_out, func[4]);
  not not_3 (not_3_out, func[3]);
  not not_4 (not_4_out, func[1]);
  not not_5 (not_5_out, func[2]);
  not not_6 (not_6_out, func[0]);
  not not_7 (not_7_out, opcode[5]);
  not not_8 (not_8_out, opcode[4]);
  not not_9 (not_9_out, opcode[3]);
  not not_10 (not_10_out, opcode[1]);
  not not_11 (not_11_out, opcode[2]);
  not not_12 (not_12_out, opcode[0]);
  and ADDU (ADDU_out, func[5], not_2_out, not_3_out, not_5_out, not_4_out, func[0], not_7_out, not_8_out, not_9_out, not_11_out, not_10_out, not_12_out);
  and SUBU (SUBU_out, func[5], not_2_out, not_3_out, not_5_out, func[1], func[0], not_7_out, not_8_out, not_9_out, not_11_out, not_10_out, not_12_out);
  and ORI (ORI_out, not_7_out, not_8_out, opcode[3], opcode[2], not_10_out, opcode[0]);
  and LW (LW_out, opcode[5], not_8_out, not_9_out, not_11_out, opcode[1], opcode[0]);
  and SW (SW_out, opcode[5], not_8_out, opcode[3], not_11_out, opcode[1], opcode[0]);
  and BEQ (BEQ_out, not_7_out, not_8_out, not_9_out, opcode[2], not_10_out, not_12_out);
  and LUI (ExtOp_1_0[1], not_7_out, not_8_out, opcode[3], opcode[2], opcode[1], opcode[0]);
  or u_RegDst (RegDst, ADDU_out, SUBU_out);
  or u_ALUSrc (ALUSrc, ORI_out, LW_out, SW_out, ExtOp_1_0[1]);
  buf u_MemtoReg (MemtoReg, LW_out);  // OR_Gate
  or u_RegWrite (RegWrite, ADDU_out, SUBU_out, ExtOp_1_0[1], ORI_out, LW_out);
  buf u_Memread (Memread, LW_out);  // OR_Gate
  buf u_MemWrite (MemWrite, SW_out);  // OR_Gate
  buf u_Branch (Branch, BEQ_out);  // OR_Gate
  buf ALUOp1 (ALUOp_1_0[1], ORI_out);  // OR_Gate
  or ALUOp0 (ALUOp_1_0[0], SUBU_out, BEQ_out);
  or ExtOp_0 (ExtOp_1_0[0], LW_out, SW_out);

  // Notes on the sheet:
  //   0
  //   1
  //   000000addu   000000subu   001101ori   100011lw   101011sw   000100beq   001111lui    000010j
  //   0
  //   1
endmodule

// RegFile(GPR)
module RegFile (
  input  clk,
  input  RegWrite,
  input  [4:0] \A1_读寄存器 ,
  input  [4:0] \A2_读寄存器 ,
  input  [4:0] \A3_写寄存器 ,
  input  [31:0] \WD要写的数据 ,
  output [31:0] \D1读出的寄存器数据 ,
  output [31:0] \D2读出的寄存器数据 
);

  wire demultiplexer_1_out0, demultiplexer_1_out1, demultiplexer_1_out2, demultiplexer_1_out3,
       demultiplexer_1_out4, demultiplexer_1_out5, demultiplexer_1_out6, demultiplexer_1_out7,
       demultiplexer_1_out8, demultiplexer_1_out9, demultiplexer_1_out10, demultiplexer_1_out11,
       demultiplexer_1_out12, demultiplexer_1_out13, demultiplexer_1_out14, demultiplexer_1_out15,
       demultiplexer_1_out16, demultiplexer_1_out17, demultiplexer_1_out18, demultiplexer_1_out19,
       demultiplexer_1_out20, demultiplexer_1_out21, demultiplexer_1_out22, demultiplexer_1_out23,
       demultiplexer_1_out24, demultiplexer_1_out25, demultiplexer_1_out26, demultiplexer_1_out27,
       demultiplexer_1_out28, demultiplexer_1_out29, demultiplexer_1_out30, demultiplexer_1_out31;
  wire [31:0] _0, _1, _2, _3, _4, _5, _6, _7, _8, _9, _10, _11, _12, _13, _14, _15, _16, _17, _18, _19, _20,
       _21, _22, _23, _24, _25, _26, _27, _28, _29, _30, _31;

  Demultiplexer #(.select(5)) demultiplexer_1 (
    .out0(demultiplexer_1_out0), .out1(demultiplexer_1_out1), .out2(demultiplexer_1_out2),
    .out3(demultiplexer_1_out3), .out4(demultiplexer_1_out4), .out5(demultiplexer_1_out5),
    .out6(demultiplexer_1_out6), .out7(demultiplexer_1_out7), .out8(demultiplexer_1_out8),
    .out9(demultiplexer_1_out9), .out10(demultiplexer_1_out10), .out11(demultiplexer_1_out11),
    .out12(demultiplexer_1_out12), .out13(demultiplexer_1_out13), .out14(demultiplexer_1_out14),
    .out15(demultiplexer_1_out15), .out16(demultiplexer_1_out16), .out17(demultiplexer_1_out17),
    .out18(demultiplexer_1_out18), .out19(demultiplexer_1_out19), .out20(demultiplexer_1_out20),
    .out21(demultiplexer_1_out21), .out22(demultiplexer_1_out22), .out23(demultiplexer_1_out23),
    .out24(demultiplexer_1_out24), .out25(demultiplexer_1_out25), .out26(demultiplexer_1_out26),
    .out27(demultiplexer_1_out27), .out28(demultiplexer_1_out28), .out29(demultiplexer_1_out29),
    .out30(demultiplexer_1_out30), .out31(demultiplexer_1_out31), .in(RegWrite), .sel(\A3_写寄存器 ));  // open: en
  // Probe on _0
  Register #(.width(32)) register_1 (.D(\WD要写的数据 ), .en(demultiplexer_1_out0), .Q(_0), .clk(clk));  // open: clr
  Register #(.width(32)) register_2 (.D(\WD要写的数据 ), .en(demultiplexer_1_out1), .Q(_1), .clk(clk));  // open: clr
  Register #(.width(32)) register_3 (.D(\WD要写的数据 ), .en(demultiplexer_1_out2), .Q(_2), .clk(clk));  // open: clr
  Register #(.width(32)) register_4 (.D(\WD要写的数据 ), .en(demultiplexer_1_out3), .Q(_3), .clk(clk));  // open: clr
  Register #(.width(32)) register_5 (.D(\WD要写的数据 ), .en(demultiplexer_1_out4), .Q(_4), .clk(clk));  // open: clr
  Register #(.width(32)) register_6 (.D(\WD要写的数据 ), .en(demultiplexer_1_out5), .Q(_5), .clk(clk));  // open: clr
  Register #(.width(32)) register_7 (.D(\WD要写的数据 ), .en(demultiplexer_1_out6), .Q(_6), .clk(clk));  // open: clr
  Register #(.width(32)) register_8 (.D(\WD要写的数据 ), .en(demultiplexer_1_out7), .Q(_7), .clk(clk));  // open: clr
  Register #(.width(32)) register_9 (.D(\WD要写的数据 ), .en(demultiplexer_1_out8), .Q(_8), .clk(clk));  // open: clr
  Register #(.width(32)) register_10 (.D(\WD要写的数据 ), .en(demultiplexer_1_out9), .Q(_9), .clk(clk));  // open: clr
  Register #(.width(32)) register_11 (.D(\WD要写的数据 ), .en(demultiplexer_1_out10), .Q(_10), .clk(clk));  // open: clr
  Register #(.width(32)) register_12 (.D(\WD要写的数据 ), .en(demultiplexer_1_out11), .Q(_11), .clk(clk));  // open: clr
  Register #(.width(32)) register_13 (.D(\WD要写的数据 ), .en(demultiplexer_1_out12), .Q(_12), .clk(clk));  // open: clr
  Register #(.width(32)) register_14 (.D(\WD要写的数据 ), .en(demultiplexer_1_out13), .Q(_13), .clk(clk));  // open: clr
  Register #(.width(32)) register_15 (.D(\WD要写的数据 ), .en(demultiplexer_1_out14), .Q(_14), .clk(clk));  // open: clr
  Register #(.width(32)) register_16 (.D(\WD要写的数据 ), .en(demultiplexer_1_out15), .Q(_15), .clk(clk));  // open: clr
  Register #(.width(32)) register_17 (.D(\WD要写的数据 ), .en(demultiplexer_1_out16), .Q(_16), .clk(clk));  // open: clr
  Register #(.width(32)) register_18 (.D(\WD要写的数据 ), .en(demultiplexer_1_out17), .Q(_17), .clk(clk));  // open: clr
  Register #(.width(32)) register_19 (.D(\WD要写的数据 ), .en(demultiplexer_1_out18), .Q(_18), .clk(clk));  // open: clr
  Register #(.width(32)) register_20 (.D(\WD要写的数据 ), .en(demultiplexer_1_out19), .Q(_19), .clk(clk));  // open: clr
  Register #(.width(32)) register_21 (.D(\WD要写的数据 ), .en(demultiplexer_1_out20), .Q(_20), .clk(clk));  // open: clr
  Register #(.width(32)) register_22 (.D(\WD要写的数据 ), .en(demultiplexer_1_out21), .Q(_21), .clk(clk));  // open: clr
  Register #(.width(32)) register_23 (.D(\WD要写的数据 ), .en(demultiplexer_1_out22), .Q(_22), .clk(clk));  // open: clr
  Register #(.width(32)) register_24 (.D(\WD要写的数据 ), .en(demultiplexer_1_out23), .Q(_23), .clk(clk));  // open: clr
  Register #(.width(32)) register_25 (.D(\WD要写的数据 ), .en(demultiplexer_1_out24), .Q(_24), .clk(clk));  // open: clr
  Register #(.width(32)) register_26 (.D(\WD要写的数据 ), .en(demultiplexer_1_out25), .Q(_25), .clk(clk));  // open: clr
  Register #(.width(32)) register_27 (.D(\WD要写的数据 ), .en(demultiplexer_1_out26), .Q(_26), .clk(clk));  // open: clr
  Register #(.width(32)) register_28 (.D(\WD要写的数据 ), .en(demultiplexer_1_out27), .Q(_27), .clk(clk));  // open: clr
  Register #(.width(32)) register_29 (.D(\WD要写的数据 ), .en(demultiplexer_1_out28), .Q(_28), .clk(clk));  // open: clr
  Register #(.width(32)) register_30 (.D(\WD要写的数据 ), .en(demultiplexer_1_out29), .Q(_29), .clk(clk));  // open: clr
  Register #(.width(32)) register_31 (.D(\WD要写的数据 ), .en(demultiplexer_1_out30), .Q(_30), .clk(clk));  // open: clr
  Register #(.width(32)) register_32 (.D(\WD要写的数据 ), .en(demultiplexer_1_out31), .Q(_31), .clk(clk));  // open: clr
  // Probe on _1
  // Probe on _5
  // Probe on _7
  // Probe on _11
  // Probe on nothing
  // Probe on _2
  // Probe on _4
  // Probe on _6
  // Probe on _8
  // Probe on _10
  // Probe on _3
  // Probe on _9
  // Probe on nothing
  // Probe on nothing
  // Probe on nothing
  // Probe on nothing
  // Probe on nothing
  // Probe on nothing
  // Probe on nothing
  // Probe on nothing
  // Probe on nothing
  // Probe on nothing
  // Probe on nothing
  // Probe on nothing
  // Probe on nothing
  // Probe on nothing
  // Probe on nothing
  // Probe on nothing
  // Probe on nothing
  // Probe on nothing
  Multiplexer #(.select(5), .width(32)) multiplexer_1 (
    .in0(_0), .in1(_1), .in2(_2), .in3(_3), .in4(_4), .in5(_5), .in6(_6), .in7(_7), .in8(_8), .in9(_9),
    .in10(_10), .in11(_11), .in12(_12), .in13(_13), .in14(_14), .in15(_15), .in16(_16), .in17(_17),
    .in18(_18), .in19(_19), .in20(_20), .in21(_21), .in22(_22), .in23(_23), .in24(_24), .in25(_25),
    .in26(_26), .in27(_27), .in28(_28), .in29(_29), .in30(_30), .in31(_31), .out(\D1读出的寄存器数据 ),
    .sel(\A1_读寄存器 ));  // open: en
  Multiplexer #(.select(5), .width(32)) multiplexer_2 (
    .in0(_0), .in1(_1), .in2(_2), .in3(_3), .in4(_4), .in5(_5), .in6(_6), .in7(_7), .in8(_8), .in9(_9),
    .in10(_10), .in11(_11), .in12(_12), .in13(_13), .in14(_14), .in15(_15), .in16(_16), .in17(_17),
    .in18(_18), .in19(_19), .in20(_20), .in21(_21), .in22(_22), .in23(_23), .in24(_24), .in25(_25),
    .in26(_26), .in27(_27), .in28(_28), .in29(_29), .in30(_30), .in31(_31), .out(\D2读出的寄存器数据 ),
    .sel(\A2_读寄存器 ));  // open: en

  // Other names for the same wires on the sheet: A1_控制读哪个寄存器[4:0] = \A1_读寄存器 ; A2_控制读哪个寄存器[4:0] = \A2_读寄存器 ;
  //   A3_控制写哪个寄存器[4:0] = \A3_写寄存器 

  // Notes on the sheet:
  //   控制写哪个寄存器
  //   控制读哪个寄存器 可以读两个
  //   Data 要写的数据
  //   控制写哪个寄存器
  //   output
  //   input
endmodule

module Extender (
  input  [15:0] imm16,
  input  [1:0] ExtOp_1_0,
  output [31:0] ext32
);

  wire [31:0] bit_extender_1_out, bit_extender_2_out;

  assign bit_extender_1_out = {{16{1'b0}}, imm16};  // Bit_Extender bit_extender_1
  assign bit_extender_2_out = {{16{imm16[15]}}, imm16};  // Bit_Extender bit_extender_2
  Multiplexer #(.select(2), .width(32)) multiplexer_1 (
    .in0(bit_extender_1_out), .in1(bit_extender_2_out), .in2({imm16, {16{1'b0}}}), .out(ext32),
    .sel(ExtOp_1_0));  // open: in3, en

  // Notes on the sheet:
  //   低16位补0
  //   lui 拓展到高16位
  //   1 0 拓展到高16位
endmodule
